// Logisim project bots.circ as structural Verilog: 1 circuit, main circuit main
module main (
  input  CURR_PLAYER,
  input  PREP_PHASE_END,
  input  CLR,
  input  CLK,
  input  WIN,
  input  [3:0] SHIPS_NUMBER,
  output ROTATED,
  output CONFIRM,
  output [3:0] X,
  output [3:0] Y
);

  wire _10SHIPS, and_1_out, and_2_out, BOOT_PHASE, comparator_1_eq, comparator_1_gt, demultiplexer_1_out0,
       demultiplexer_1_out1, demultiplexer_1_out2, not_1_out, not_3_out, or_2_out, or_3_out, POSITION_CLOCK,
       random_1_out, ROTATION_CLOCK, SHOOT_PHASE, SHOT_DONE;
  wire [3:0] main_1_output, main_2_output;
  wire [4:0] counter_1_q;

  Clock clock_1 ();  // open: out
  not not_1 (not_1_out, PREP_PHASE_END);
  not not_2 (not_1_out, PREP_PHASE_END);
  not not_3 (not_3_out, _10SHIPS);
  and and_1 (and_1_out, BOOT_PHASE, CLK);
  and and_2 (and_2_out, CURR_PLAYER, ~BOOT_PHASE, PREP_PHASE_END, ~WIN);  // AND_Gate
  and and_3 (BOOT_PHASE, not_1_out, not_3_out);
  Comparator #(.width(4), .mode("unsigned")) comparator_1 (
    .a(SHIPS_NUMBER), .b(4'b1010), .gt(comparator_1_gt), .eq(comparator_1_eq));  // open: lt
  Demultiplexer #(.select(5)) demultiplexer_1 (
    .out0(demultiplexer_1_out0), .out1(demultiplexer_1_out1), .out2(demultiplexer_1_out2), .in(1'b1),
    .sel(counter_1_q));  // open: out3, out4, out5, out6, out7, out8, out9, out10, out11, out12, out13, out14, out15, out16, out17, out18, out19, out20, out21, out22, out23, out24, out25, out26, out27, out28, out29, out30, out31, en
  Counter #(.width(5), .max('h1f)) counter_1 (
    .Q(counter_1_q), .clk(and_1_out), .clr(CLR));  // open: load, D, count, carry
  or or_1 (_10SHIPS, comparator_1_gt, comparator_1_eq);
  or or_2 (or_2_out, and_2_out, or_3_out);
  or or_3 (or_3_out, SHOT_DONE, WIN);
  assign ROTATION_CLOCK = and_1_out ? demultiplexer_1_out0 : 1'bz;  // Controlled_Buffer controlled_buffer_1
  assign POSITION_CLOCK = and_1_out ? demultiplexer_1_out1 : 1'bz;  // Controlled_Buffer controlled_buffer_2
  assign CONFIRM = and_1_out ? demultiplexer_1_out2 : 1'bz;  // Controlled_Buffer controlled_buffer_3
  S_R_Flip_Flop s_r_ff_1 (.S(and_2_out), .clk(or_2_out), .R(or_3_out), .Q(SHOOT_PHASE));  // open: Qn, preset, reset, en
  Pull_Resistor pull_resistor_1 (.node(ROTATION_CLOCK));
  Pull_Resistor pull_resistor_2 (.node(POSITION_CLOCK));
  Counter #(.width(1), .max('h1)) counter_2 (
    .Q(ROTATED), .clk(random_1_out), .clr(CLR));  // open: load, D, count, carry
  Random #(.width(1)) random_1 (.clk(ROTATION_CLOCK), .next(ROTATION_CLOCK), .out(random_1_out));  // open: clr
  Pull_Resistor pull_resistor_3 (.node(CONFIRM));
  random_num_generator_A_main main_1 (.GENERATE(POSITION_CLOCK), .OUTPUT(main_1_output));
  random_num_generator_B_main main_2 (.GENERATE(POSITION_CLOCK), .OUTPUT(main_2_output));
  bot_0_main main_3 (
    .in_1(CLK), .in_2(SHOOT_PHASE), .in_3(SHOOT_PHASE), .CONFIRM(CONFIRM), .X(X), .Y(Y), .out_6(SHOT_DONE));
  assign X = BOOT_PHASE ? main_1_output : 4'bz;  // Controlled_Buffer controlled_buffer_4
  assign Y = BOOT_PHASE ? main_2_output : 4'bz;  // Controlled_Buffer controlled_buffer_5

  // Other names for the same wires on the sheet: CONFIRM_CLOCK = CONFIRM; SHIP_NUMBER[3:0] = SHIPS_NUMBER
endmodule
