// Logisim project memory_management.circ as structural Verilog: 1 circuit, main circuit main
module main (
  input  [3:0] X,
  input  [3:0] Y,
  input  ROTATED,
  output [14:0] RAM_OUT
);

  wire CLK_out, CONFIRM, main_1_p3, main_3_p5, main_3_p6, main_4_p5, not_1_out;
  wire [3:0] CURRENT_SHIP;
  wire [14:8] SHIP_DATA;

  Button u_CONFIRM (.out(CONFIRM));
  Multiplexer #(.select(2), .width(4), .enable("false")) multiplexer_1 (
    .in0(4'b0001), .in1(4'b0011), .in2(4'b0111), .in3(4'b1111), .out(SHIP_DATA[14:11]), .sel(SHIP_DATA[9:8]));
  assign RAM_OUT = CONFIRM ? {SHIP_DATA[14:11], ROTATED, SHIP_DATA[9:8], Y, X} : 15'bz;  // Controlled_Buffer controlled_buffer_1
  not not_1 (not_1_out, CONFIRM);
  Clock CLK (.out(CLK_out));
  RAM #(.addrWidth(4), .dataWidth(15)) ram_1 (
    .addr(CURRENT_SHIP), .data(RAM_OUT), .clk(CLK_out), .ld(not_1_out));  // open: sel, clr
  Counter #(.width(4), .max('h9), .trigger("falling")) counter_1 (
    .Q(CURRENT_SHIP), .clk(CONFIRM));  // open: load, D, count, carry, clr
  // _4bit_greater_or_equal_than_and_less_than_main main_1: pin names not known; wires that end beside it: CURRENT_SHIP, 4'b0000, main_1_p3
  // _4bit_greater_or_equal_than_and_less_than_main main_2: pin names not known; wires that end beside it: 4'b0100, CURRENT_SHIP
  // _4bit_greater_or_equal_than_and_less_than_main main_3: pin names not known; wires that end beside it: 4'b0100, 4'b0111, CURRENT_SHIP, 4'b0111, main_3_p5, main_3_p6
  // _4bit_greater_or_equal_than_and_less_than_main main_4: pin names not known; wires that end beside it: 4'b1001, CURRENT_SHIP, 4'b1001, 4'b1010, main_4_p5
  assign SHIP_DATA[9:8] = main_1_p3 ? 2'b00 : 2'bz;  // Controlled_Buffer controlled_buffer_2
  Pull_Resistor pull_resistor_1 (.node(SHIP_DATA[9:8]));
  assign SHIP_DATA[9:8] = main_3_p5 ? 2'b01 : 2'bz;  // Controlled_Buffer controlled_buffer_3
  Pull_Resistor pull_resistor_2 (.node(SHIP_DATA[9:8]));
  Pull_Resistor pull_resistor_3 (.node(SHIP_DATA[9:8]));
  assign SHIP_DATA[9:8] = main_3_p6 ? 2'b10 : 2'bz;  // Controlled_Buffer controlled_buffer_4
  assign SHIP_DATA[9:8] = main_4_p5 ? 2'b11 : 2'bz;  // Controlled_Buffer controlled_buffer_5
  Pull_Resistor pull_resistor_4 (.node(SHIP_DATA[9:8]));

  // Other names for the same wires on the sheet: SHIP_DATA (some bits) = {ROTATED, Y, X}; SHIP_X[3:0] = X;
  //   SHIP_Y[3:0] = Y; SHIP_TYPE[1:0] = SHIP_DATA[9:8]; IS_ROTATED = ROTATED
endmodule
