// Logisim project not_hit_ram_storage.circ as structural Verilog: 1 circuit, main circuit main
module main (
  input  IF_1__save_input,
  input  in_2,
  input  [3:0] X,
  input  [3:0] Y,
  output [3:0] X_2,
  output [3:0] Y_2
);

  wire and_1_out, CLK, clock_1_out, d_ff_1_q, d_ff_1_qn, d_ff_2_q, not_1_out, STORE;
  wire [7:0] ADDRESS, DATA, STABLE_COUNTER_q;

  Clock u_CLK (.out(CLK));
  Counter #(.max('h90)) STABLE_COUNTER (
    .Q(STABLE_COUNTER_q), .clk(IF_1__save_input), .clr(in_2));  // open: load, D, count, carry
  Register register_1 (.D({Y, X}), .Q(DATA), .clk(IF_1__save_input));  // open: en, clr
  Clock clock_1 (.out(clock_1_out));
  Comparator comparator_1 (.a(STABLE_COUNTER_q), .b(ADDRESS), .eq(STORE));  // open: gt, lt
  D_Flip_Flop d_ff_1 (.clk(clock_1_out), .D(STORE), .Q(d_ff_1_q), .Qn(d_ff_1_qn));  // open: preset, en, reset
  not not_1 (not_1_out, clock_1_out);
  Counter #(.max('h90)) UNSTABLE_COUNTER (.Q(ADDRESS), .clk(CLK), .clr(and_1_out));  // open: load, D, count, carry
  D_Flip_Flop d_ff_2 (.clk(not_1_out), .D(d_ff_1_qn), .Q(d_ff_2_q));  // open: Qn, preset, en, reset
  // NOT_Gate not_2 is placed but not wired
  and and_1 (and_1_out, d_ff_1_q, d_ff_2_q);
  RAM #(.bus("separate")) ram_1 (
    .addr(ADDRESS), .din(DATA), .data({Y_2, X_2}), .str(STORE), .clk(CLK), .ld(1'b1));  // open: sel, clr
endmodule
